# Fritzing sketch RGB (saved by Fritzing 0.9.3b)
breadboards: 1

parts:
  R1 = Resistor [tolerance=±5% resistance=220 package=THT]
  R2 = Resistor [tolerance=±5% resistance=220 package=THT]
  R3 = Resistor [tolerance=±5% resistance=220 package=THT]
  R4 = Resistor [tolerance=±5% resistance=220 package=THT]
  R5 = Resistor [tolerance=±5% resistance=220 package=THT]
  R6 = Resistor [tolerance=±5% resistance=220 package=THT]
  LED1 = RGB LED (com. cathode, rgb) [package="5 mm [THT]"]
  LED2 = RGB LED (com. cathode, rgb) [package="5 mm [THT]"]
  Parça1 = Arduino Uno (Rev3) - ICSP

nets:
  N1: R1.Pin_0, Parça1.D10_PWM/SS
  N2: R1.Pin_1, LED2.green_anode
  N3: R2.Pin_0, Parça1.D5_PWM
  N4: R2.Pin_1, LED1.green_anode
  N5: R3.Pin_0, Parça1.D6_PWM
  N6: R3.Pin_1, LED1.red_anode
  N7: R4.Pin_0, Parça1.D11_PWM/MOSI
  N8: R4.Pin_1, LED2.red_anode
  N9: R5.Pin_0, Parça1.D9_PWM
  N10: R5.Pin_1, LED2.blue_anode
  N11: R6.Pin_0, Parça1.D3_PWM
  N12: R6.Pin_1, LED1.blue_anode
  N13: LED1.common_cathode, LED2.common_cathode, Parça1.GND
